# Fritzing sketch SparkNode-Custom (saved by Fritzing 0.7.11b)

parts:
  U1 = atmega328 [package=dip]
  XTAL1 = Crystal [frequency="16 Mhz" package=THT]
  R1 = Resistor [tolerance=±5% resistance=220 package=THT]
  RFM12b1 = RFM12b HopeRF Transceiver
  U2 = MCP1702 Voltage Regulator [package="TO92 [THT]"]
  C1 = Ceramic Capacitor [capacitance=100nF package="100 mil [THT, multilayer]"]
  LED1 = LED - 3mm [color="Red (633nm)" package="3 mm [THT]"]
  R2 = Resistor [tolerance=±5% resistance=150 package=THT]
  Part1 = FTDI Basic Programmer
  J1 = female pin header, 3 pins [form="♀ (female)" part_number=RX-868]

nets:
  N1: U1.RESET, R1.Pin_1, C1.1
  N2: U1.D0_(RX), Part1.TXO
  N3: U1.D1_(TX), Part1.RXI
  N4: U1.D2, RFM12b1.2_nIRQ
  N5: U1.VCC, U1.AVCC, U1.AREF, R1.Pin_0, RFM12b1.9_VDD, U2.Vout, J1.pin2
  GND: U1.GND, RFM12b1.7_GND, RFM12b1.10_GND, U2.GND, LED1.cathode, Part1.GND, J1.pin3
  N6: U1.XLAT1, XTAL1.pin_0
  N7: U1.XLAT2, XTAL1.pin_1
  N8: U1.D10_(PWM), RFM12b1.14_nSEL
  N9: U1.D11_(PWM), RFM12b1.12_SDI
  N10: U1.D12, RFM12b1.1_SDO
  N11: U1.D13, RFM12b1.13_SCK, R2.Pin_0
  N12: U1.A0, J1.pin1
  N13: U2.Vin, Part1.POWER
  N14: C1.0, Part1.DTR
  N15: LED1.anode, R2.Pin_1

custom parts:
  RFM12b HopeRF Transceiver: RF Transceiver by Hope RF. Well supported Arduino libraries are available. Part is available in several frequencies (433MHz, 915MHz)...
  MCP1702 Voltage Regulator: A MCP1702 Low Dropout Fixed Voltage Regulator (available in 1.2V, 1.5V, 1.8V, 2.5V, 2.8V, 3.0V, 3.3V, 4.0V, 5.0V)
