# Fritzing sketch SparkNode-JeeNode (saved by Fritzing 0.7.11b)

parts:
  LED1 = LED - 3mm [color="Red (633nm)" package="3 mm [THT]"]
  R2 = Resistor [tolerance=±5% resistance=150 package=THT]
  Part1 = FTDI Basic Programmer
  J1 = female pin header, 3 pins [form="♀ (female)" part_number=RX-868]
  Part2 = JeeNode wireless microcontroller

nets:
  GND: LED1.cathode, Part1.GND, J1.pin3, Part2.GND
  N1: LED1.anode, R2.Pin_1
  N2: R2.Pin_0, Part2.SCK
  N3: Part1.DTR, Part2.DTR
  N4: Part1.RXI, Part2.TXD
  N5: Part1.TXO, Part2.RXD
  N6: Part1.POWER, Part2.PWX
  N7: Part1.CTS, Part2.N/C
  N8: J1.pin1, Part2.A0
  N9: J1.pin2, Part2.VCC
